// Logisim project lab4-practice.circ as structural Verilog: 1 circuit, main circuit main
module main (
  input  H,
  input  L,
  input  E
);

  wire HE_out, HL_out, LE_out, or_1_out;

  and LE (LE_out, E, L);
  and HE (HE_out, H, E);
  or or_1 (or_1_out, LE_out, HE_out, HL_out);
  and HL (HL_out, L, H);
  LED led_1 (.in(or_1_out));
endmodule
