// Logisim project lab4.circ as structural Verilog: 1 circuit, main circuit main
module main (
  input  A,
  input  B,
  input  C
);

  wire and_1_out, or_1_out;

  and and_1 (and_1_out, A, or_1_out);
  LED led_1 ();  // open: in
  or or_1 (or_1_out, C, B);

  // Notes on the sheet:
  //   A(B +C)
endmodule
