// Logisim project Lab5P2.circ as structural Verilog: 1 circuit, main circuit main
module main (
  input  A,
  input  B
);

  // XOR_Gate SUM has open pins: in0=A, in1=B, out=open
  // AND_Gate Cout has open pins: in0=A, in1=B, out=open
endmodule
