// Logisim project Lab5P4.circ as structural Verilog: 1 circuit, main circuit main
module main (
  input  A,
  input  B,
  input  Cin,
  input  in_4,
  input  in_5,
  input  in_6,
  input  in_7,
  input  in_8,
  input  in_9
);

  wire and_1_out, and_2_out, and_3_out, and_4_out, and_5_out, and_6_out, and_7_out, and_8_out, or_1_out,
       or_2_out, or_3_out, or_4_out, xor_1_out, xor_2_out, xor_3_out, xor_4_out, xor_5_out, xor_6_out,
       xor_7_out, xor_8_out;

  xor xor_1 (xor_1_out, A, B);
  and and_1 (and_1_out, A, B);
  xor xor_2 (xor_2_out, xor_1_out, Cin);
  and and_2 (and_2_out, xor_1_out, Cin);
  or or_1 (or_1_out, and_2_out, and_1_out);
  xor xor_3 (xor_3_out, in_4, in_5);
  and and_3 (and_3_out, in_4, in_5);
  xor xor_4 (xor_4_out, xor_3_out, or_1_out);
  and and_4 (and_4_out, xor_3_out, or_1_out);
  or or_2 (or_2_out, and_4_out, and_3_out);
  xor xor_5 (xor_5_out, in_6, in_7);
  and and_5 (and_5_out, in_6, in_7);
  xor xor_6 (xor_6_out, xor_5_out, or_2_out);
  and and_6 (and_6_out, xor_5_out, or_2_out);
  or or_3 (or_3_out, and_6_out, and_5_out);
  xor xor_7 (xor_7_out, in_8, in_9);
  and and_7 (and_7_out, in_8, in_9);
  xor xor_8 (xor_8_out, xor_7_out, or_3_out);
  and and_8 (and_8_out, xor_7_out, or_3_out);
  or or_4 (or_4_out, and_8_out, and_7_out);

  // Notes on the sheet:
  //   SUM
  //   A XOR B
  //   Sum
  //   SUM
  //   Cout
  //   A XOR B
  //   Sum
  //   SUM
  //   Cout
  //   A XOR B
  //   Sum
  //   SUM
  //   Cout
  //   A XOR B
  //   Sum
  //   Cout
endmodule
