// Logisim project Lab_5_PT1_FINAL.circ as structural Verilog: 1 circuit, main circuit main
module main (
  input  in_1
);

  wire A_q, A_qn, and_1_out, and_2_out, and_3_out, and_4_out, and_5_out, and_6_out, and_7_out, and_8_out,
       and_9_out, and_10_out, and_11_out, B_q, C_q, C_qn, clock_1_out, D_q, or_1_out, or_2_out, or_3_out,
       or_4_out;
  wire [3:0] undriven;

  Clock clock_1 (.out(clock_1_out));
  or or_1 (or_1_out, and_4_out, and_5_out);
  or or_2 (or_2_out, and_8_out, and_9_out);
  or or_3 (or_3_out, and_10_out, and_11_out);
  and and_1 (and_1_out, A_qn, C_q, D_q);
  or or_4 (or_4_out, and_6_out, and_7_out);
  and and_2 (and_2_out, A_qn, B_q, C_q, D_q);
  and and_3 (and_3_out, C_q, D_q);
  and and_4 (and_4_out, B_q, C_q);
  and and_5 (and_5_out, A_qn, C_q, D_q);
  and and_6 (and_6_out, C_qn, D_q);
  and and_7 (and_7_out, A_q, B_q, C_qn);
  and and_8 (and_8_out, A_q, C_q);
  and and_9 (and_9_out, C_q, D_q);
  and and_10 (and_10_out, C_q, D_q, A_qn);
  and and_11 (and_11_out, C_q, A_q, B_q);
  J_K_Flip_Flop A (
    .J(and_2_out), .K(and_3_out), .clk(clock_1_out), .Q(A_q), .Qn(A_qn), .preset(undriven[3]));  // open: reset
  J_K_Flip_Flop B (
    .J(or_1_out), .K(and_1_out), .clk(clock_1_out), .Q(B_q), .Qn(B_q), .preset(undriven[2]));  // open: reset
  J_K_Flip_Flop C (
    .J(or_4_out), .K(or_2_out), .clk(clock_1_out), .Q(C_q), .Qn(C_qn), .preset(undriven[1]));  // open: reset
  Hex_Digit_Display hex_digit_display_1 (.value(undriven));  // open: dp
  J_K_Flip_Flop D (.J(or_3_out), .K(in_1), .clk(clock_1_out), .Q(D_q), .Qn(D_q), .preset(undriven[0]));  // open: reset

  // Notes on the sheet:
  //   KC
  //   JD
  //   JC
  //   JA
  //   KA
  //   JB
  //   KB
endmodule
