// Logisim project Lab_5_PT2.circ as structural Verilog: 1 circuit, main circuit main
module main (
  input  [3:0] in_1,
  input  [3:0] in_2
);

  wire clock_1_out;
  wire [3:0] adder_1_out, register_1_q;

  Clock clock_1 (.out(clock_1_out));
  Adder #(.width(4)) adder_1 (.a(in_1), .b(in_2), .out(adder_1_out));  // open: cin, cout
  Register #(.width(4)) register_1 (.D(adder_1_out), .en(1'b1), .clk(clock_1_out), .Q(register_1_q));  // open: clr
  Hex_Digit_Display hex_digit_display_1 (.value(register_1_q));  // open: dp
endmodule
