// Logisim project FullAddr.circ as structural Verilog: 1 circuit, main circuit main
module main (
  input  in_1,
  input  in_2,
  input  in_3
);

  wire and_1_out, xor_1_out, xor_2_out;

  ExactlyOne xor_1 (.out(xor_1_out), .in0(in_1), .in1(in_3), .in2(in_2));
  xor xor_2 (xor_2_out, in_1, in_2);
  and and_1 (and_1_out, in_3, xor_2_out);
  // OR_Gate or_1 has open pins: in0=xor_1_out, in1=and_1_out, out=open
endmodule
