// Logisim project RSFlipFlop.circ as structural Verilog: 1 circuit, main circuit main
module main (
  input  in_1,
  input  in_2
);

  wire clock_1_out, nor_1_out, nor_2_out, nor_3_out, nor_4_out;

  Clock clock_1 (.out(clock_1_out));
  nor nor_1 (nor_1_out, in_1, clock_1_out);
  nor nor_2 (nor_2_out, clock_1_out, in_2);
  nor nor_3 (nor_3_out, nor_4_out, nor_2_out);
  nor nor_4 (nor_4_out, nor_1_out, nor_3_out);
  LED led_1 (.in(nor_4_out));
  LED led_2 (.in(nor_3_out));

  // Notes on the sheet:
  //   S
  //   R
  //   Q
  //   !Q
endmodule
