// Logisim project SRLatachNAND.circ as structural Verilog: 1 circuit, main circuit main
module main (
  input  S,
  input  in_2
);

  wire nand_1_out, nand_2_out;

  nand nand_1 (nand_1_out, S, nand_2_out);
  nand nand_2 (nand_2_out, nand_1_out, in_2);
  LED led_1 (.in(nand_1_out));
  LED led_2 (.in(nand_2_out));

  // Notes on the sheet:
  //   R
  //   Q
  //   !Q
endmodule
